# Fritzing sketch robot_arm_circuit (saved by Fritzing 0.9.3b)

parts:
  부품1 = Arduino Nano (Rev3.0)
  J1 = Basic Servo
  U5 = SWITCH_SPDT [package=kps-1290]
  U6 = SWITCH_SPDT [package=kps-1290]
  부품2 = Adafruit PCA9685 PWM/Servo Breakout [part_number=815]
  부품3 = Thumb Joystick
  J2 = Basic Servo
  J3 = Basic Servo
  J4 = Basic Servo
  J5 = Basic Servo
  J6 = Basic Servo
  M1 = RioRand LM2596
  부품4 = Thumb Joystick
  부품5 = Thumb Joystick
  VCC2 = 4 x AAA Battery Mount
  VCC3 = Battery

nets:
  GND: 부품1.GND, J1.gnd, 부품2.GND, 부품2.OE, 부품3.GND, J2.gnd, J3.gnd, J4.gnd, J5.gnd, J6.gnd, M1.Pin_4, 부품4.GND, 부품5.GND, VCC2.-
  N1: 부품1.VIN, U6.P
  VCC: 부품1.5V, J1.vcc, 부품2.5.0V, 부품2.VCC, 부품3.VCC, J2.vcc, J3.vcc, J4.vcc, J5.vcc, J6.vcc, 부품4.VCC, 부품5.VCC
  N2: 부품1.A7, 부품3.VERT
  N3: 부품1.A6, 부품3.HORZ
  N4: 부품1.A5, 부품2.SCL
  N5: 부품1.A4, 부품2.SDA
  N6: 부품1.A3, 부품4.VERT
  N7: 부품1.A2, 부품4.HORZ
  N8: 부품1.A1, 부품5.VERT
  N9: 부품1.A0, 부품5.HORZ
  N10: J1.pulse, 부품2.PWM0
  N11: U5.O, M1.Pin_1
  N12: U5.P, VCC3.+
  N13: U6.O, VCC2.+
  N14: 부품2.PWRIN, M1.Pin_3
  N15: 부품2.PWM5, J6.pulse
  N16: 부품2.PWM4, J5.pulse
  N17: 부품2.PWM3, J4.pulse
  N18: 부품2.PWM2, J3.pulse
  N19: 부품2.PWM1, J2.pulse
  N20: M1.Pin_2, VCC3.-

custom parts:
  Adafruit PCA9685 PWM/Servo Breakout: Using only two pins, control 16 free-running PWM outputs! I2C-controlled PWM driver with a built in clock. Unlike the TLC5940 family, you do not need to continuously send it signal tying up your microcontroller, its completely free running! 5V compliant, which means you can control it from a 3.3V microcontroller and still safely drive up to 6V outputs (this is good for when you want to control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
  Battery: Your standard 2x 18650 battery pack (14.7 Volts)
